# Fritzing sketch 5x5x6 led cube diagram (saved by Fritzing 0.9.0b)
breadboards: 3

parts:
  IC9 = IC, DIP package, 20 pins [chip_label=74LS245]
  IC16 = IC, DIP package, 20 pins [chip_label=74LS245]
  IC12 = IC, DIP package, 20 pins [chip_label=74LS245]
  IC4 = IC, DIP package, 20 pins [chip_label=74LS245]
  IC13 = IC, DIP package, 20 pins [chip_label=74LS245]
  IC1 = IC, DIP package, 20 pins [chip_label=74LS245]
  IC11 = IC, DIP package, 20 pins [chip_label=74LS245]
  IC15 = IC, DIP package, 20 pins [chip_label=74LS245]
  IC14 = IC, DIP package, 20 pins [chip_label=74LS245]
  IC10 = IC, DIP package, 20 pins [chip_label=74LS245]
  IC3 = IC, DIP package, 20 pins [chip_label=74LS245]
  IC2 = IC, DIP package, 20 pins [chip_label=74LS245]
  Part1 = Arduino Uno (Rev3)

nets:
  N1: IC9.pin2, IC16.pin2, IC1.pin2, IC14.pin2, IC10.pin2, IC3.pin2, Part1.D1/TX
  N2: IC9.pin3, IC16.pin3, IC1.pin3, IC14.pin3, IC10.pin3, IC3.pin3, Part1.D2
  N3: IC9.pin4, IC16.pin4, IC1.pin4, IC14.pin4, IC10.pin4, IC3.pin4, Part1.D3_PWM
  N4: IC9.pin5, IC16.pin5, IC1.pin5, IC14.pin5, IC10.pin5, IC3.pin5, Part1.D4
  N5: IC9.pin6, IC16.pin6, IC1.pin6, IC14.pin6, IC10.pin6, IC3.pin6, Part1.D6_PWM
  N6: IC9.pin7, IC16.pin7, IC1.pin7, IC14.pin7, IC10.pin7, IC3.pin7, Part1.D7
  N7: IC9.pin8, IC16.pin8, IC1.pin8, IC14.pin8, IC10.pin8, IC3.pin8, Part1.D8
  N8: IC9.pin9, IC16.pin9, IC1.pin9, IC14.pin9, IC10.pin9, IC3.pin9, Part1.D9_PWM
  N9: IC9.pin19, IC11.pin19, Part1.A2
  N10: IC9.pin20, IC12.pin20, IC10.pin20
  N11: IC16.pin19, IC13.pin19, Part1.A0
  N12: IC16.pin20, IC15.pin20, IC14.pin20
  N13: IC12.pin1, IC11.pin1, IC10.pin1
  N14: IC12.pin2, IC4.pin2, IC13.pin2, IC11.pin2, IC15.pin2, IC2.pin2, Part1.D5_PWM
  N15: IC12.pin3, IC4.pin3, IC13.pin3, IC11.pin3, IC15.pin3, IC2.pin3, Part1.D10_PWM/SS
  N16: IC12.pin19, IC10.pin19, Part1.A3
  N17: IC4.pin1, IC1.pin1, IC3.pin1, IC2.pin1
  N18: IC4.pin10, IC1.pin10, IC3.pin10, IC2.pin10
  N19: IC4.pin19, IC3.pin19, Part1.A5/SCL
  N20: IC4.pin20, IC1.pin20, IC3.pin20
  N21: IC13.pin1, IC15.pin1, IC14.pin1
  N22: IC13.pin10, IC14.pin10
  N23: IC1.pin19, IC2.pin19, Part1.A4/SDA
  N24: IC11.pin10, IC10.pin10
  N25: IC15.pin19, IC14.pin19, Part1.A1
