# Fritzing sketch 5x5x6 led cube schematic (saved by Fritzing 0.9.0b)
breadboards: 1

parts:
  Part1 = Arduino Uno (Rev3)
  IC1 = IC, DIP package, 20 pins [chip_label=74LS245]
  IC2 = IC, DIP package, 20 pins [chip_label=74LS245]
  IC3 = IC, DIP package, 20 pins [chip_label=74LS245]
  IC4 = IC, DIP package, 20 pins [chip_label=74LS245]
  IC5 = IC, DIP package, 20 pins [chip_label=74LS245]
  IC6 = IC, DIP package, 20 pins [chip_label=74LS245]
  IC7 = IC, DIP package, 20 pins [chip_label=74LS245]
  IC8 = IC, DIP package, 20 pins [chip_label=74LS245]
  IC9 = IC, DIP package, 20 pins [chip_label=74LS245]
  IC10 = IC, DIP package, 20 pins [chip_label=74LS245]
  IC11 = IC, DIP package, 20 pins [chip_label=74LS245]
  IC12 = IC, DIP package, 20 pins [chip_label=74LS245]

nets:
  N1: Part1.A0, IC1.pin19, IC2.pin19
  N2: Part1.A1, IC3.pin19, IC4.pin19
  N3: Part1.A2, IC6.pin19, IC7.pin19
  N4: Part1.A3, IC5.pin19, IC8.pin19
  N5: Part1.A4/SDA, IC11.pin19, IC12.pin19
  N6: Part1.D8, IC1.pin8, IC3.pin8
  N7: Part1.D9_PWM, IC1.pin9, IC3.pin9
  N8: Part1.D10_PWM/SS, IC2.pin3, IC4.pin3
  N9: Part1.A5/SCL, IC9.pin19, IC10.pin19
  N10: Part1.D1/TX, IC1.pin2, IC3.pin2
  N11: Part1.D2, IC1.pin3, IC3.pin3
  N12: Part1.D3_PWM, IC1.pin4, IC3.pin4
  N13: Part1.D4, IC1.pin5, IC3.pin5
  N14: Part1.D5_PWM, IC2.pin2, IC4.pin2
  N15: Part1.D6_PWM, IC1.pin6, IC3.pin6
  N16: Part1.D7, IC1.pin7, IC3.pin7
  N17: IC5.pin2, IC6.pin2
  N18: IC5.pin3, IC6.pin3
  N19: IC5.pin4, IC6.pin4
  N20: IC5.pin5, IC6.pin5
  N21: IC5.pin6, IC6.pin6
  N22: IC5.pin7, IC6.pin7
  N23: IC5.pin8, IC6.pin8
  N24: IC5.pin9, IC6.pin9
  N25: IC7.pin2, IC8.pin2
  N26: IC7.pin3, IC8.pin3
  N27: IC9.pin2, IC12.pin2
  N28: IC9.pin3, IC12.pin3
  N29: IC10.pin2, IC11.pin2
  N30: IC10.pin3, IC11.pin3
  N31: IC10.pin4, IC11.pin4
  N32: IC10.pin5, IC11.pin5
  N33: IC10.pin6, IC11.pin6
  N34: IC10.pin7, IC11.pin7
  N35: IC10.pin8, IC11.pin8
  N36: IC10.pin9, IC11.pin9
